// Logisim project Lab3_Procesador_Monociclo.circ as structural Verilog: 3 circuits, main circuit main
module main (
);

  IFetch ifetch_1 ();  // open: nextPC, CLK, Reset, PCplus4, Instruction
endmodule

module IFetch (
  input  [31:0] nextPC,
  input  CLK,
  input  Reset,
  output [31:0] PCplus4,
  output [31:0] Instruction
);

  wire [1:0] register_1_q, register_1_q_2, register_1_q_3, register_1_q_4, register_1_q_5, register_1_q_6,
       register_1_q_7, register_1_q_8, register_1_q_9, register_1_q_10, register_1_q_11, register_1_q_12,
       register_1_q_13, register_1_q_14, register_1_q_15, register_1_q_16;

  Register #(.width(32)) register_1 (
    .D(nextPC), .clk(CLK),
    .Q({register_1_q_8, register_1_q_7, register_1_q_6, register_1_q_5, register_1_q_4, register_1_q_3, register_1_q_2, register_1_q_16, register_1_q_15, register_1_q_14, register_1_q_13, register_1_q_12, register_1_q_11, register_1_q_10, register_1_q_9, register_1_q}),
    .clr(Reset));  // open: en
  Adder #(.width(32)) adder_1 (
    .a(32'h4),
    .b({register_1_q_8, register_1_q_7, register_1_q_6, register_1_q_5, register_1_q_4, register_1_q_3, register_1_q_2, register_1_q_16, register_1_q_15, register_1_q_14, register_1_q_13, register_1_q_12, register_1_q_11, register_1_q_10, register_1_q_9, register_1_q}),
    .out(PCplus4));  // open: cin, cout
  ROM #(.addrWidth(16), .dataWidth(32)) rom_1 (
    .addr({register_1_q_16, register_1_q_15, register_1_q_14, register_1_q_13, register_1_q_12, register_1_q_11, register_1_q_10, register_1_q_9}),
    .data(Instruction));
endmodule

module ISplit (
  input  [31:0] Instruction,
  output [5:0] funct,
  output address
);


  assign funct = Instruction[5:0];
endmodule
